// Logisim project OMGSAMWORKS.circ as structural Verilog: 1 circuit, main circuit main
module main (
  output [7:0] out_1
);

  wire Add_out, and_1_out, and_2_out, and_3_out, and_4_out, and_5_out, and_6_out, and_7_out, and_8_out,
       and_9_out, clock_1_out, Clr_out, decoder_1_out0, decoder_1_out1, decoder_1_out2, decoder_1_out3,
       Hlt_out, Jaz_out, Jmp_out, Lda_out, not_2_out, not_3_out, not_4_out, not_5_out, not_6_out, not_7_out,
       not_8_out, not_9_out, or_1_out, or_2_out, or_3_out, or_4_out, Out_3_out, Sta_out;
  wire [1:0] counter_1_q;
  wire [3:0] IR_2_q, MAR_q, multiplexer_1_out, not_1_out, PC_2_q;
  wire [7:0] ACC_q, adder_1_out, multiplexer_2_out, ram_1_data, xor_1_out;
  wire [7:4] IR_2_q_2;
  wire [7:7] Sub_2_out;

  Button Clr (.out(Clr_out));
  Clock clock_1 (.out(clock_1_out));
  and and_1 (and_1_out, clock_1_out, Hlt_out);
  LED PC (.in(and_2_out));
  and and_2 (and_2_out, decoder_1_out2, or_1_out);
  or or_1 (or_1_out, Jmp_out, and_8_out);
  Counter #(.width(4), .max('hf)) PC_2 (
    .load(and_2_out), .D(IR_2_q), .count(decoder_1_out0), .Q(PC_2_q), .clk(and_1_out), .clr(Clr_out));  // open: carry
  LED Inc (.in(decoder_1_out0));
  Counter #(.width(2), .max('h3)) counter_1 (
    .Q(counter_1_q), .clk(and_1_out), .clr(Clr_out));  // open: load, D, count, carry
  Multiplexer #(.width(4), .enable("false")) multiplexer_1 (
    .in0(PC_2_q), .in1(IR_2_q), .out(multiplexer_1_out), .sel(and_3_out));
  LED AMux (.in(and_3_out));
  and and_3 (and_3_out, decoder_1_out2, or_3_out);
  Decoder #(.select(2), .enable("false")) decoder_1 (
    .out0(decoder_1_out0), .out1(decoder_1_out1), .out2(decoder_1_out2), .out3(decoder_1_out3),
    .sel(counter_1_q));
  Register #(.width(4)) MAR (.D(multiplexer_1_out), .en(or_2_out), .Q(MAR_q), .clk(and_1_out));  // open: clr
  LED MAR_2 (.in(or_2_out));
  or or_2 (or_2_out, decoder_1_out0, and_3_out);
  LED Mst (.in(and_4_out));
  and and_4 (and_4_out, decoder_1_out3, Sta_out);
  or or_3 (or_3_out, or_4_out, Sta_out);
  RAM #(.addrWidth(4), .bus("separate")) ram_1 (
    .addr(MAR_q), .din(ACC_q), .data(ram_1_data), .str(and_4_out), .clk(and_1_out));  // open: sel, ld, clr
  LED IR (.in(decoder_1_out1));
  Multiplexer #(.width(8), .enable("false")) multiplexer_2 (
    .in0(adder_1_out), .in1(ram_1_data), .out(multiplexer_2_out), .sel(and_5_out));
  LED DMux (.in(and_5_out));
  and and_5 (and_5_out, decoder_1_out3, Lda_out);
  Register ACC (.D(multiplexer_2_out), .en(and_6_out), .Q(ACC_q), .clk(and_1_out));  // open: clr
  Register IR_2 (.D(ram_1_data), .en(decoder_1_out1), .Q({IR_2_q_2, IR_2_q}), .clk(and_1_out), .clr(Clr_out));
  LED Acc_2 (.in(and_6_out));
  and and_6 (and_6_out, decoder_1_out3, or_4_out);
  Register OUT (.D(ACC_q), .en(and_7_out), .Q(out_1), .clk(and_1_out));  // open: clr
  LED Out_2 (.in(and_7_out));
  and and_7 (and_7_out, decoder_1_out2, Out_3_out);
  or or_4 (or_4_out, Lda_out, Add_out, Sub_2_out[7]);
  LED Sub (.in(Sub_2_out[7]));
  and and_8 (and_8_out, and_9_out, Jaz_out);
  assign xor_1_out = ram_1_data ^ {8{Sub_2_out[7]}};  // XOR_Gate xor_1, 8 bits wide
  and Lda (Lda_out, not_1_out[3], not_1_out[2], not_1_out[1], not_1_out[0]);
  and Add (Add_out, not_1_out[3], not_1_out[2], not_1_out[1], IR_2_q_2[4]);
  and Sub_2 (Sub_2_out[7], not_1_out[3], not_1_out[2], IR_2_q_2[5], not_1_out[0]);
  and Sta (Sta_out, not_1_out[3], not_1_out[2], IR_2_q_2[5], IR_2_q_2[4]);
  and Jmp (Jmp_out, not_1_out[3], IR_2_q_2[6], not_1_out[1], not_1_out[0]);
  and Jaz (Jaz_out, not_1_out[3], IR_2_q_2[6], not_1_out[1], IR_2_q_2[4]);
  and Out_3 (Out_3_out, IR_2_q_2[7], IR_2_q_2[6], IR_2_q_2[5], not_1_out[0]);
  nand Hlt (Hlt_out, IR_2_q_2[7], IR_2_q_2[6], IR_2_q_2[5], IR_2_q_2[4]);
  Adder adder_1 (.a(ACC_q), .b(xor_1_out), .out(adder_1_out), .cin(Sub_2_out[7]));  // open: cout
  assign not_1_out = ~IR_2_q_2;  // NOT_Gate not_1, 4 bits wide
  not not_2 (not_2_out, ACC_q[7]);
  not not_3 (not_3_out, ACC_q[6]);
  not not_4 (not_4_out, ACC_q[5]);
  not not_5 (not_5_out, ACC_q[4]);
  not not_6 (not_6_out, ACC_q[3]);
  not not_7 (not_7_out, ACC_q[2]);
  and and_9 (and_9_out, not_2_out, not_3_out, not_4_out, not_5_out, not_6_out, not_7_out, not_8_out, not_9_out);
  not not_8 (not_8_out, ACC_q[1]);
  not not_9 (not_9_out, ACC_q[0]);

  // Notes on the sheet:
  //   PC
  //   RT State
  //   AMUX
  //   DMUX
  //   Jaz Check Logic
endmodule
